# Fritzing sketch montagem (saved by Fritzing 0.9.6b)

parts:
  U1 = NodeMCU V3.0
  M1 = fc-51 [package=THT]
  LED1 = Red LED - Rect 5x2x7mm [package="5x2x7 mm [THT]"]  # not connected
  OLED_I2C1 = OLED 128x64 I2C Monochrome Display
  LED2 = Green LED - Rect 5x2x7mm [package="5x2x7 mm [THT]"]  # not connected
  RE1 = KY-040 Rotary encoder [package=THT]
  R1 = Resistor [tolerance=±5% power=0.25 resistance=150 package=THT]
  R2 = Resistor [tolerance=±5% power=0.25 resistance=150 package=THT]

nets:
  N1: U1.D0, M1.pin1, R2.Pin_0
  N2: U1.D1, OLED_I2C1.SCK
  N3: U1.D2, OLED_I2C1.SDA
  N4: U1.D3, R1.Pin_1
  N5: U1.D5, RE1.SW
  N6: U1.D6, RE1.DT
  N7: U1.D7, RE1.CLK
  GND: U1.GND, RE1.GND
  3V3: U1.3V3, RE1.Vcc, R2.Pin_1

custom parts:
  NodeMCU V3.0: NodeMcu V3 Lua WIFI Development Board
  Red LED - Rect 5x2x7mm: A generic rectangular red LED (~1.8V) 5mm x 2mm x 7mm
  Green LED - Rect 5x2x7mm: A generic rectangular green LED (~1.8V) 5mm x 2mm x 7mm
  KY-040 Rotary encoder: KY-040 Rotary Encoder with switch on breakout borad from AZ Delivery
